// Digital circuit rjstack.dig as structural Verilog
module rjstack (
  input  clk,
  output [15:0] ros,
  output [15:0] tos,
  output [11:0] sp,
  output [15:0] nos,
  output [15:0] y,
  output [7:0] i,
  output [7:0] pc
);

  wire comparator_1_eq, multiplexer_2_out, not_1_out;
  wire [1:0] microcode_d_2;
  wire [5:0] microcode_d;
  wire [7:0] add_1_s, multiplexer_1_out, program_d;
  wire [15:0] bitextender_1_out;

  Multiplexer #(.Bits(8)) multiplexer_1 (.sel(multiplexer_2_out), .in_0(8'h1), .in_1(i), .out(multiplexer_1_out));
  Add #(.Bits(8)) add_1 (.a(pc), .b(multiplexer_1_out), .c_i(1'b0), .s(add_1_s));  // open: c_o
  ROM #(.AddrBits(8), .Bits(16)) \program  (.A(pc), .sel(1'b1), .D({i, program_d}));
  not not_1 (not_1_out, comparator_1_eq);
  Multiplexer #(.Selector_Bits(2)) multiplexer_2 (
    .sel(microcode_d_2), .in_0(1'b0), .in_1(1'b1), .in_2(comparator_1_eq), .in_3(not_1_out),
    .out(multiplexer_2_out));
  Register #(.Bits(8)) u_pc (.D(add_1_s), .C(clk), .en(~microcode_d[5]), .Q(pc));
  ROM #(.AddrBits(8), .Bits(8)) microcode (.A(program_d), .sel(1'b1), .D({microcode_d_2, microcode_d}));
  LED push (.in(microcode_d[0]));
  LED pop (.in(microcode_d[1]));
  LED i__gt_tos (.in(microcode_d[2]));
  LED nos__gt_tos (.in(microcode_d[3]));
  LED y__gt_tos (.in(microcode_d[4]));
  LED halt (.in(microcode_d[5]));
  BitExtender bitextender_1 (.in(i), .out(bitextender_1_out));
  stack stack_1 (
    .clk(clk), .push(microcode_d[0]), .pop(microcode_d[1]), .we_itos(microcode_d[2]),
    .we_nostos(microcode_d[3]), .we_ytos(microcode_d[4]), .i(bitextender_1_out), .y(y), .sp(sp), .ros(ros),
    .nos(nos), .tos(tos));
  Add #(.Bits(16)) alu (.a(nos), .b(tos), .c_i(1'b0), .s(y));  // open: c_o
  Comparator #(.Bits(16)) comparator_1 (.a(tos), .b({16{1'b0}}), .eq(comparator_1_eq));  // open: gt, lt

  // Other names for the same wires on the sheet: c = clk

  // Notes on the sheet:
  //   clk: Hz: 20
  //   [03]
  //   FPGA Stack Machine CPU from Scratch
  //   contents of program (hex, n*v repeats v):
  //   101,201,2,401,2,f901,2,206,8,1,101,3,206,8,f205
  //   contents of microcode (hex, n*v repeats v):
  //   0,5,12,a,9,40,80,c0,20
  //   Halt and Catch Fire
  //   rj45Creates
endmodule
